# Fritzing sketch arduino_dac_iv (saved by Fritzing 0.9.10b)
circuit board: 8.46667cm x 5.64444cm
breadboards: 1

parts:
  DAC = DIP - 8 pins [package="DIP (Dual Inline) [THT]"]
  Arduino = Arduino Uno (Rev3)
  Transistor = MOSFET-NCHANNEL [package=to220v]
  Solarzelle = SOLAR-IXYS [package=solarbit-12x1]
  R1 = Resistor [tolerance=±5% power=0.25 resistance=10 package=THT]

nets:
  N1: DAC.V_DD, Arduino.5V
  N2: DAC.CS, Arduino.D10_PWM/SS
  N3: DAC.SCK, Arduino.D13/SCK
  N4: DAC.SDI, Arduino.D11_PWM/MOSI
  N5: DAC.LDAC, DAC.V_SS, Arduino.GND, Solarzelle.C, R1.Pin_1
  N6: DAC.V_Out_A, Transistor.G
  N7: Arduino.A0, Transistor.D, Solarzelle.A
  N8: Arduino.A1, Transistor.S, R1.Pin_0

custom parts:
  DIP - 8 pins: MCP4822 - DAC
